# Fritzing sketch esp32-breadboard-wiring (saved by Fritzing 0.9.3b)
breadboards: 2

parts:
  LED2 = RGB LED (com. anode, rbg) [package="5 mm [THT]"]
  M2 = BMP280
  VCC1 = Battery
  Bauteil2 = BH1750
  KY-2 = Keyes Relay [package=THT]
  YL-83_-_Detection_Board2 = YL-83 Rain Sensor - Detection Board
  YL-83_-_Control_Board2 = YL-83 Rain Sensor - Control Board
  U2 = ESP32-38PinWide [part_number=ESP32-38PinWide]
  M3 = DC Motor

nets:
  GND: LED2.red_cathode, M2.GND, Bauteil2.GND, KY-2.ground, YL-83_-_Control_Board2.GND, U2.GND
  N1: LED2.common_anode, U2.GPIO19
  N2: LED2.blue_cathode, U2.GPIO18
  N3: LED2.green_cathode, U2.GPIO17
  VIN: M2.VIN, Bauteil2.VCC, U2.3.3
  N4: M2.SCL, Bauteil2.SCL, U2.GPIO21
  N5: M2.SDA, Bauteil2.SDA, U2.GPIO22
  N6: VCC1.+, KY-2.NO
  N7: KY-2.signal, U2.GPIO25
  VCC: KY-2.power, YL-83_-_Control_Board2.VCC, U2.VIN
  N8: KY-2.C, M3.pin_1
  N9: YL-83_-_Detection_Board2.POS, YL-83_-_Control_Board2.POS
  N10: YL-83_-_Detection_Board2.NEG, YL-83_-_Control_Board2.NEG
  N11: YL-83_-_Control_Board2.AO, U2.GPIO32

notes:
  3x AA = 4.5V
  Stromkabel: Gelb: Alles oberhalb nutzt 5V alles unterhalb des Boards 3.3V
  Ground: Braun
  Pumpe: Farben können nicht geändert werden. In echt sind die auch rot/schwarz. Es gilt: Schwarz an Batterie (schwarz) und rot ans Relais.
  Analoge Sensoren: Daten lila, s. Readme
  Relais: Lila Steuerung
  Digitale Sensoren: blau SDA, grün SCL
  Board: (v.l.n.r.)
  Belegung oben:
  5V, GND, 25, 33,32,3V
  Belegung unten:
  G17,G18,G19.G21,G22, GND
  ACHTUNG: NICHT GND neben 5V nutzen! Falsch bedruckt, dann wird das Board nicht angehen.
  Board-Belegung:
  oben - Minus
  unten + Plus

custom parts:
  BMP280: Temperature Humidity Barometric presure Sensor, I2C
  BH1750: Light Sensor
  Keyes Relay: The Keyes 5V relay module is suitable for SCM development, home appliance control. It uses a 5V~12V TIL control signal which can control DC / AC signal.
  YL-83 Rain Sensor - Detection Board: The YL-83 is a rain sensor that has more resistance when dry and less resistance when wet. The module runs at 5V.
  YL-83 Rain Sensor - Control Board: The YL-83 is a rain sensor that has more resistance when dry and less resistance when wet. The module runs at 5V.
  ESP32-38PinWide: Generic 38-Pin ESP32 with wide format (only access to one side of pins on a breadboard) based on Stephen Lilley's HiLetgo ESP-WROOM-32 ESP32 ESP-32S Development Board.
